# Fritzing sketch Photocell-und-Servo (saved by Fritzing 0.7.4b)
breadboards: 1

parts:
  R4 = Resistor [resistance=10k tolerance=±5% package=THT]
  R5 = Photocell (LDR) [package=THT]
  Arduino1 = Arduino
  J1 = Basic Servo
  S1 = Pushbutton [package=THT]

nets:
  N1: R4.Pin_0, R5.pin_1, Arduino1.A2
  GND: R4.Pin_1, Arduino1.GND, J1.gnd, S1.leg0
  N2: R5.pin_0, Arduino1.+5V
  N3: Arduino1.D9, J1.pulse
  N4: Arduino1.D2, S1.leg1
